# Fritzing sketch irweb (saved by Fritzing 0.9.2b)
breadboards: 1

parts:
  part = NodeMCU V1.0
  IR_LED_(OSI5LA5113A) = LED - 5mm [color="Infrared (940nm)" package="5 mm [THT]"]
  LED(ＧＬ８ＥＤ４８) = LED - 3mm [color="Green (555nm)" package="3 mm [THT]"]
  LED(ＧＬ８ＥＤ４８)_2 = LED - 3mm [color="Orange (605nm)" package="3 mm [THT]"]
  PUSH_BUTTON = Pushbutton [package=THT]
  IR_RECEIVER_(GP1UXC41QS) = Infra red receiver

nets:
  N1: part.D1, PUSH_BUTTON.leg0
  3V3: part.3V3, IR_RECEIVER_(GP1UXC41QS).VCC
  GND: part.GND, IR_RECEIVER_(GP1UXC41QS).GND
  N2: part.D5, IR_RECEIVER_(GP1UXC41QS).Data
  N3: part.D6, IR_LED_(OSI5LA5113A).anode
  N4: part.D7, LED(ＧＬ８ＥＤ４８).anode
  N5: part.D8, LED(ＧＬ８ＥＤ４８)_2.anode
  N6: IR_LED_(OSI5LA5113A).cathode, LED(ＧＬ８ＥＤ４８).cathode, LED(ＧＬ８ＥＤ４８)_2.cathode, PUSH_BUTTON.leg1

custom parts:
  NodeMCU V1.0: ESP9266 based NodeMCU
